# Fritzing sketch schematic (saved by Fritzing 0.7.4b)
breadboards: 1

parts:
  U1 = Arduino Mega
  right_front2 = Infrared Proximity Sensor
  Back3 = Infrared Proximity Sensor
  left_front2 = Infrared Proximity Sensor
  left_back2 = Infrared Proximity Sensor
  right_back2 = Infrared Proximity Sensor
  front2 = Infrared Proximity Sensor
  U8 = mystery part, 4 pins [chip_label=Motor spacing=300mil]
  caster = Basic Servo
  Part3 = Triple Axis Magnetometer - HMC5883 Breakout
  Part4 = Tri-Axis Gyro Breakout - L3G4200D
  pan = Basic Servo
  U9 = mystery part, 3 pins [chip_label=UVTRON spacing=300mil]
  U10 = mystery part, 3 pins [chip_label=flame spacing=300mil]
  U11 = mystery part, 4 pins [chip_label=line spacing=300mil]
  R9 = Resistor [tolerance=±5% resistance=200 package=THT]
  R10 = Resistor [tolerance=±5% resistance=5.6k package=THT]
  U12 = mystery part, 3 pins [chip_label=relay spacing=300mil]
  U13 = Voltage Regulator - 5V [package="TO220 [THT]"]
  DC_Power1 = DC Power [voltage=12]
  C1 = Electrolytic Capacitor [capacitance=10µF package="100 mil [THT, electrolytic]"]
  C2 = Electrolytic Capacitor [capacitance=10µF package="100 mil [THT, electrolytic]"]
  C3 = Electrolytic Capacitor [capacitance=0.1mF package="100 mil [THT, electrolytic]"]
  R11 = Resistor [tolerance=±5% resistance=10k package=THT]
  start_button = Pushbutton [package="[THT]"]

nets:
  N1: U1.D11, pan.pulse
  N2: U1.D9, caster.pulse
  N3: U1.D5, U11.pin3, R10.Pin_0
  N4: U1.D3, U9.pin3
  VCC: U1.3V3, Part3.VCC, Part4.VCC
  5V: U1.+5V, right_front2.Vcc, Back3.Vcc, left_front2.Vcc, left_back2.Vcc, right_back2.Vcc, front2.Vcc, caster.vcc, pan.vcc, U9.pin2, U10.pin3, R9.Pin_1, R10.Pin_1, U12.pin1, U13.output_voltage, C1.+, C2.+, start_button.Pin_3, start_button.Pin_4
  GND: U1.GND, right_front2.GND, Back3.GND, left_front2.GND, left_back2.GND, right_back2.GND, front2.GND, U8.pin1, caster.gnd, Part3.GND, Part4.GND, pan.gnd, U9.pin1, U10.pin2, U11.pin1, U11.pin4, U12.pin3, U13.GND, DC_Power1.GND, C1.-, C2.-, C3.-, R11.Pin_1
  N5: U1.A0, left_back2.Vout
  N6: U1.A1, left_front2.Vout
  N7: U1.A2, right_back2.Vout
  N8: U1.A3, right_front2.Vout
  N9: U1.A4, front2.Vout
  N10: U1.A5, Back3.Vout
  N11: U1.D18, U8.pin3
  N12: U1.D20, Part3.SDA, Part4.SDA
  N13: U1.D21, Part3.SCL, Part4.SCL
  N14: U1.D25, U12.pin2
  N15: U1.D29, R11.Pin_0, start_button.Pin_1, start_button.Pin_2
  N16: U1.A7, U10.pin1
  N17: U11.pin2, R9.Pin_0
  N18: U13.input_voltage, DC_Power1.V+, C3.+

notes:
  SDL and SCL are analog pins 4 and 5 on the arduino duemilenove, but D20 and D21 on the mega.
  both sdl and scl should already have pullup resistors on the arduino
  J1,J2,J3,J4 select how many signal pulses have to be detected consecutively inorder for the UVTRON to send a signal.
  digital pin 3 is interrupt 1.
  line sensor is actually just a ir transmitter and a phototransistor in one package.
  200ohm pullup powers the ir transmitter. (200ohm to 2000ohm will do)
  5.6kohm pullup resistor acts as a voltage divider with the phototransistor. this can be adjusted to change values(4.7k to 5.6k will do)
  the output of the collector voltage needs to be greater than 1.1V for the analog comparator to work.
  D5 is AIN1
  wiring the battery to the motor controller
  backwards will break it.
  if we end up using Li po batteries, we will have to put the 3rd switch in the down position in order to enable lithium cutoff.
  higher input voltages for the uvtron may be necessary, but I remember it working well off of 5V
  the relay I have may end up drawing too much current.
  the servos and the relay should go on their own power bus, since they can be wired in the same way
  Distance sensors, flame sensor, and line sensor can all go on the same power bus, since they all follow the order signal, gnd vcc
  6 distance sensors: 6*33mA
  1 flame sensor ? 7mA
  1 line follower 20mA
  2 servos 2*12mA at rest, 2*250mA
  1 uvtron 4mA
  1 magnetometer negligible
  1 arduino mega 20mA
  max current draw from 5V regulator: around 700mA
  bypass capacitor to stabilize power supply
  put capacitors here to filter 5V regulator's output
  pulled high when pressed.
